# Fritzing sketch schematic_fritzing (saved by Fritzing 0.9.2b)

parts:
  Bean = LightBlue Bean
  Push-button = Pushbutton [package="[SMD]"]

nets:
  N1: Bean.D0, Bean.1#86, Bean.1#90, Push-button.Pin_3, Push-button.Pin_4
  N2: Bean.1#92, Bean.1#97, Bean.1#100, Bean.GND, Push-button.Pin_1, Push-button.Pin_2
